// Logisim project add_sub.circ as structural Verilog: 1 circuit, main circuit main
module main (
  input  cin,
  input  [15:0] dataa,
  input  dir,
  input  [15:0] datab,
  input  enable,
  output [15:0] result,
  output cout,
  output overflow
);

  wire [15:0] adder_1_out, xor_1_out;
  wire [16:16] not_1_out;

  assign xor_1_out = ~{16{dir}} ^ datab;  // XOR_Gate xor_1, 16 bits wide
  not not_1 (not_1_out[16], dir);
  // Probe on {not_1_out[16], xor_1_out}
  Adder #(.width(17)) adder_1 (
    .a({1'b0, dataa}), .b({not_1_out[16], xor_1_out}), .out({cout, adder_1_out}), .cin(cin));  // open: cout
  assign result = enable ? adder_1_out : 16'bz;  // Controlled_Buffer controlled_buffer_1

  assign overflow = 1'b0;
endmodule
