// Logisim project alu.circ as structural Verilog: 1 circuit, main circuit main
module main (
  input  [15:0] data,
  input  yin,
  input  clock,
  input  aclr,
  input  zin,
  input  zinadd,
  input  [3:0] ir,
  input  zout
);

  Register #(.width(16)) y (.D(data), .en(yin), .clk(clock), .clr(aclr));  // open: Q
endmodule
