// Logisim project control_unit.circ as structural Verilog: 1 circuit, main circuit main
module main (
  input  aclr,
  input  clock,
  input  [15:0] ir
);

  wire and_1_out, nor_1_out, or_1_out, sclr_q;
  wire [2:0] multiplexer_1_out;
  wire [3:0] counter_1_q;
  wire [7:0] rom_1_data;

  D_Flip_Flop sclr (.D(nor_1_out), .Q(sclr_q));  // open: clk, Qn, preset, reset
  or or_1 (or_1_out, sclr_q, aclr);
  Counter #(.max('hf), .width(4)) counter_1 (
    .clr(or_1_out), .load(1'b0), .up(1'b1), .count(1'b1), .clk(clock), .Q(counter_1_q));  // open: D, carry
  Multiplexer #(.width(3)) multiplexer_1 (.in0(ir[5:3]), .in1(ir[2:0]), .out(multiplexer_1_out), .sel(rom_1_data[0]));
  Multiplexer #(.width(3)) multiplexer_2 (.in0(ir[5:3]), .in1(ir[2:0]), .sel(rom_1_data[4]));  // open: out
  ROM #(.addrWidth(14)) rom_1 (.addr({ir[15:6], counter_1_q}), .data(rom_1_data));
  and and_1 (and_1_out, rom_1_data[3], rom_1_data[2]);
  Decoder #(.select(3)) decoder_1 (
    .sel(multiplexer_1_out), .en(and_1_out));  // open: out0, out1, out2, out3, out4, out5, out6, out7
  nor nor_1 (nor_1_out, rom_1_data[0], rom_1_data[1], rom_1_data[2], rom_1_data[3], rom_1_data[4], rom_1_data[5], rom_1_data[6], rom_1_data[7]);
endmodule
