// Logisim project cpu.circ as structural Verilog: 14 circuits, main circuit cpu
module main (
);

  cpu cpu_1 ();  // open: clock, aclr, busy, intr, marin, ramin, ramout
  memory memory_1 ();  // open: data, ramin, marin, clock, aclr, ramout, q
endmodule

module reg16 (
  input  regout,
  input  [15:0] data,
  input  regin,
  input  clock,
  input  aclr,
  output [15:0] q,
  output [15:0] qbus
);

  Register #(.width(16)) register_1 (.D(data), .en(regin), .clk(clock), .Q(q), .clr(aclr));
  Hex_Digit_Display hex_digit_display_1 (.value(q[15:12]));  // open: dp
  Hex_Digit_Display hex_digit_display_2 (.value(q[11:8]));  // open: dp
  assign qbus = regout ? q : 16'bz;  // Controlled_Buffer controlled_buffer_1
  Hex_Digit_Display hex_digit_display_3 (.value(q[7:4]));  // open: dp
  Hex_Digit_Display hex_digit_display_4 (.value(q[3:0]));  // open: dp
endmodule

module program_counter (
  input  aclr,
  input  pcin,
  input  cnt_en,
  input  clock,
  input  pcout,
  input  [15:0] data,
  output [15:0] q
);

  wire [15:0] counter_1_q;

  // Probe on data
  Counter #(.max('hffff), .width(16)) counter_1 (
    .clr(aclr), .load(pcin), .up(1'b1), .count(cnt_en), .clk(clock), .D(data), .Q(counter_1_q));  // open: carry
  assign q = pcout ? counter_1_q : 16'bz;  // Controlled_Buffer controlled_buffer_1
endmodule

module jump_controller (
  input  [15:0] flags,
  input  pcinun,
  input  pcin,
  input  [3:0] ir,
  output jump_enable
);

  wire and_1_out, multiplexer_1_out, not_1_out, not_2_out, not_3_out, not_4_out, not_5_out, not_6_out,
       not_7_out, not_8_out, or_1_out, or_2_out, xor_1_out;

  not not_1 (not_1_out, flags[0]);
  not not_2 (not_2_out, flags[2]);
  not not_3 (not_3_out, flags[6]);
  not not_4 (not_4_out, flags[7]);
  not not_5 (not_5_out, flags[11]);
  or or_1 (or_1_out, flags[0], flags[6]);
  xor xor_1 (xor_1_out, flags[7], flags[11]);
  not not_6 (not_6_out, or_1_out);
  not not_7 (not_7_out, xor_1_out);
  or or_2 (or_2_out, xor_1_out, flags[6]);
  not not_8 (not_8_out, or_2_out);
  Multiplexer #(.select(4)) multiplexer_1 (
    .in0(flags[11]), .in1(not_5_out), .in2(flags[0]), .in3(not_1_out), .in4(flags[7]), .in5(not_4_out),
    .in6(or_1_out), .in7(not_6_out), .in8(flags[6]), .in9(not_3_out), .in10(flags[2]), .in11(not_2_out),
    .in12(xor_1_out), .in13(not_7_out), .in14(or_2_out), .in15(not_8_out), .out(multiplexer_1_out), .sel(ir));
  and and_1 (and_1_out, pcin, multiplexer_1_out);
  or or_3 (jump_enable, pcinun, and_1_out);
endmodule

module flags_register (
  input  flagsout,
  input  [15:0] flags,
  input  [15:0] data,
  input  flagsin,
  input  zin,
  input  clock,
  input  aclr,
  output [15:0] q,
  output [15:0] qbus
);

  wire or_1_out;
  wire [15:0] multiplexer_1_out;

  Multiplexer #(.width(16)) multiplexer_1 (.in0(flags), .in1(data), .out(multiplexer_1_out), .sel(flagsin));
  or or_1 (or_1_out, flagsin, zin);
  Register #(.width(16)) register_1 (.D(multiplexer_1_out), .en(or_1_out), .clk(clock), .Q(q), .clr(aclr));
  assign qbus = flagsout ? q : 16'bz;  // Controlled_Buffer controlled_buffer_1
endmodule

module control_unit (
  input  [15:0] ir,
  input  clock,
  input  aclr,
  input  busy,
  output [47:0] control,
  output ucounterrst
);

  wire and_1_out, and_2_out, and_3_out, d_ff_1_q, nand_1_out, not_2_out, or_1_out, or_2_out;
  wire [2:0] multiplexer_1_out, multiplexer_2_out;
  wire [3:0] counter_1_q;
  wire [7:0] rom_1_data;
  wire [13:0] register_1_q;

  not not_1 (ucounterrst, or_2_out);
  D_Flip_Flop d_ff_1 (.D(ucounterrst), .clk(clock), .Q(d_ff_1_q), .reset(aclr));  // open: Qn, preset
  nand nand_1 (nand_1_out, busy, control[9]);
  or or_1 (or_1_out, aclr, and_1_out);
  and and_1 (and_1_out, d_ff_1_q, ucounterrst);
  Counter #(.max('hf), .width(4)) counter_1 (
    .clr(or_1_out), .load(1'b0), .up(1'b1), .count(nand_1_out), .clk(clock), .Q(counter_1_q));  // open: D, carry
  Multiplexer #(.width(3)) multiplexer_1 (.in0(ir[5:3]), .in1(ir[2:0]), .out(multiplexer_1_out), .sel(rom_1_data[4]));
  Multiplexer #(.width(3)) multiplexer_2 (.in0(ir[5:3]), .in1(ir[2:0]), .out(multiplexer_2_out), .sel(rom_1_data[0]));
  or or_2 (or_2_out, rom_1_data[0], rom_1_data[1], rom_1_data[2], rom_1_data[3], rom_1_data[4], rom_1_data[5], rom_1_data[6], rom_1_data[7]);
  Register #(.width(14)) register_1 (
    .D({ir[15:6], counter_1_q}), .en(1'b1), .clk(not_2_out), .Q(register_1_q), .clr(aclr));
  not not_2 (not_2_out, clock);
  Decoder #(.select(3)) decoder_1 (
    .out0(control[40]), .out1(control[41]), .out2(control[42]), .out3(control[43]), .out4(control[44]),
    .out5(control[45]), .out6(control[46]), .out7(control[47]), .sel(multiplexer_1_out), .en(and_2_out));
  and and_2 (and_2_out, rom_1_data[5], rom_1_data[6], rom_1_data[7]);
  and and_3 (and_3_out, rom_1_data[1], rom_1_data[2], rom_1_data[3]);
  Decoder #(.select(3)) decoder_2 (
    .out0(control[32]), .out1(control[33]), .out2(control[34]), .out3(control[35]), .out4(control[36]),
    .out5(control[37]), .out6(control[38]), .out7(control[39]), .sel(multiplexer_2_out), .en(and_3_out));
  ROM #(.addrWidth(14)) rom_1 (.addr(register_1_q), .data(rom_1_data));
  Decoder #(.select(4)) decoder_3 (
    .out0(control[0]), .out1(control[1]), .out2(control[2]), .out3(control[3]), .out4(control[4]),
    .out5(control[5]), .out6(control[6]), .out7(control[7]), .out8(control[8]), .out9(control[9]),
    .out10(control[10]), .out11(control[11]), .out12(control[12]), .out13(control[13]), .out14(control[14]),
    .out15(control[15]), .sel(rom_1_data[3:0]), .en(or_2_out));
  Decoder #(.select(4)) decoder_4 (
    .out0(control[16]), .out1(control[17]), .out2(control[18]), .out3(control[19]), .out4(control[20]),
    .out5(control[21]), .out6(control[22]), .out7(control[23]), .out8(control[24]), .out9(control[25]),
    .out10(control[26]), .out11(control[27]), .out12(control[28]), .out13(control[29]), .out14(control[30]),
    .out15(control[31]), .sel(rom_1_data[7:4]), .en(or_2_out));

  // Notes on the sheet:
  //   contents of rom_1 (hex, n*v repeats v):
  //   4 51 14*0 4 51 14*0 4 51 14*0 4 51 14*0 4 51 f4 56 e7 75 10*0 4 51 4 52 24 56 e7 75 8*0 4 51 4 52 f6
  //   28 74 56 e7 75 6*0 4 51 f6 e7 7f 11*0 4 51 14*0 4 51 14*0 4 51 14*0 4 51 14*0 4 51 e6 f4 57 7e 10*0
  //   4 51 4 52 e6 24 57 7e 8*0 4 51 4 52 f6 28 74 e6 57 7e 6*0 4 51 e6 f7 7e 11*0 4 51 14*0 4 51 14*0 4
  //   51 14*0 4 51 14*0 4 51 4 52 f4 56 27 75 8*0 4 51 4 52 4 53 24 56 37 75 6*0 4 51 4 52 4 53 f6 28 74
  //   56 37 75 4*0 4 51 4 52 f6 27 7f 9*0 4 51 14*0 4 51 14*0 4 51 14*0 4 51 14*0 4 51 14*0 4 51 14*0 4 51
  //   14*0 4 51 14*0 4 51 14*0 4 51 14*0 4 51 14*0 4 51 14*0 4 51 f4 56 e7 75 10*0 4 51 4 52 24 56 e7 75
  //   8*0 4 51 4 52 f6 28 74 56 e7 75 6*0 4 51 f6 e7 7f 11*0 4 51 14*0 4 51 14*0 4 51 14*0 4 51 14*0 4 51
  //   e6 f4 57 7e 10*0 4 51 4 52 e6 24 57 7e 8*0 4 51 4 52 f6 28 74 e6 57 7e 6*0 4 51 e6 f7 7e 11*0 4 51
  //   14*0 4 51 14*0 4 51 14*0 4 51 14*0 4 51 4 52 f4 56 27 75 8*0 4 51 4 52 4 53 24 56 37 75 6*0 4 51 4
  //   52 4 53 f6 28 74 56 37 75 4*0 4 51 4 52 f6 27 7f 9*0 4 51 14*0 4 51 14*0 4 51 14*0 4 51 14*0 4 51
  //   14*0 4 51 14*0 4 51 14*0 4 51 14*0 4 51 14*0 4 51 14*0 4 51 14*0 4 51 14*0 4 51 14*0 4 51 14*0 4 51
  //   14*0 4 51 14*0 4 51 14*0 4 51 14*0 4 51 14*0 4 51 14*0 4 51 14*0 4 51 14*0 4 51 14*0 4 51 14*0 4 51
  //   14*0 4 51 14*0 4 51 14*0 4 51 14*0 4 51 14*0 4 51 14*0 4 51 14*0 4 51 14*0 4 51 14*0 4 51 14*0 4 51
  //   14*0 4 51 14*0 4 51 14*0 4 51 14*0 4 51 14*0 4 51 14*0 4 51 14*0 4 51 14*0 4 51 14*0 4 51 14*0 4 51
  //   14*0 4 51 14*0 4 51 14*0 4 51 14*0 4 51 14*0 4 51 14*0 4 51 14*0 4 51 14*0 4 51 14*0 4 51 14*0 4 51
  //   14*0 4 51 14*0 4 51 14*0 4 51 14*0 4 51 14*0 4 51 14*0 4 51 14*0 4 51 14*0 4 51 14*0 4 51 14*0 4 51
  //   14*0 4 51 14*0 4 51 14*0 4 51 14*0 4 51 14*0 4 51 14*0 4 51 14*0 4 51 14*0 4 51 14*0 4 51 14*0 4 51
  //   14*0 4 51 14*0 4 51 f4 56 e7 75 10*0 4 51 4 52 24 56 e7 75 8*0 4 51 4 52 f6 28 74 56 e7 75 6*0 4 51
  //   f6 e7 7f 11*0 4 51 14*0 4 51 14*0 4 51 14*0 4 51 14*0 4 51 e6 f4 57 7e 10*0 4 51 4 52 e6 24 57 7e
  //   8*0 4 51 4 52 f6 28 74 e6 57 7e 6*0 4 51 e6 f7 7e 11*0 4 51 14*0 4 51 14*0 4 51 14*0 4 51 14*0 4 51
  //   4 52 f4 56 27 75 8*0 4 51 4 52 4 53 24 56 37 75 6*0 4 51 4 52 4 53 f6 28 74 56 37 75 4*0 4 51 4 52
  //   f6 27 7f 9*0 4 51 14*0 4 51 14*0 4 51 14*0 4 51 14*0 4 51 14*0 4 51 14*0 4 51 14*0 4 51 14*0 4 51
  //   14*0 4 51 14*0 4 51 14*0 4 51 14*0 4 51 f4 56 e7 75 10*0 4 51 4 52 24 56 e7 75 8*0 4 51 4 52 f6 28
  //   74 56 e7 75 6*0 4 51 f6 e7 7f 11*0 4 51 14*0 4 51 14*0 4 51 14*0 4 51 14*0 4 51 e6 f4 57 7e 10*0 4
  //   51 4 52 e6 24 57 7e 8*0 4 51 4 52 f6 28 74 e6 57 7e 6*0 4 51 e6 f7 7e 11*0 4 51 14*0 4 51 14*0 4 51
  //   14*0 4 51 14*0 4 51 4 52 f4 56 27 75 8*0 4 51 4 52 4 53 24 56 37 75 6*0 4 51 4 52 4 53 f6 28 74 56
  //   37 75 4*0 4 51 4 52 f6 27 7f 9*0 4 51 14*0 4 51 14*0 4 51 14*0 4 51 14*0 4 51 14*0 4 51 14*0 4 51
  //   14*0 4 51 14*0 4 51 14*0 4 51 14*0 4 51 14*0 4 51 14*0 4 51 f4 56 e7 75 10*0 4 51 4 52 24 56 e7 75
  //   8*0 4 51 4 52 f6 28 74 56 e7 75 6*0 4 51 f6 e7 7f 11*0 4 51 14*0 4 51 14*0 4 51 14*0 4 51 14*0 4 51
  //   e6 f4 57 7e 10*0 4 51 4 52 e6 24 57 7e 8*0 4 51 4 52 f6 28 74 e6 57 7e 6*0 4 51 e6 f7 7e 11*0 4 51
  //   14*0 4 51 14*0 4 51 14*0 4 51 14*0 4 51 4 52 f4 56 27 75 8*0 4 51 4 52 4 53 24 56 37 75 6*0 4 51 4
  //   52 4 53 f6 28 74 56 37 75 4*0 4 51 4 52 f6 27 7f 9*0 4 51 14*0 4 51 14*0 4 51 14*0 4 51 14*0 4 51
  //   14*0 4 51 14*0 4 51 14*0 4 51 14*0 4 51 14*0 4 51 14*0 4 51 14*0 4 51 14*0 4 51 f4 56 e7 11*0 4 51 4
  //   52 24 56 e7 9*0 4 51 4 52 f6 28 74 56 e7 7*0 4 51 f6 e7 12*0 4 51 14*0 4 51 14*0 4 51 14*0 4 51 14*0
  //   4 51 e6 f4 57 11*0 4 51 4 52 e6 24 57 9*0 4 51 4 52 f6 28 74 e6 57 7*0 4 51 e6 f7 12*0 4 51 14*0 4
  //   51 14*0 4 51 14*0 4 51 14*0 4 51 4 52 f4 56 27 9*0 4 51 4 52 4 53 24 56 37 7*0 4 51 4 52 4 53 f6 28
  //   74 56 37 5*0 4 51 4 52 f6 27 10*0 4 51 14*0 4 51 14*0 4 51 14*0 4 51 14*0 4 51 14*0 4 51 14*0 4 51
  //   14*0 4 51 14*0 4 51 14*0 4 51 14*0 4 51 14*0 4 51 14*0 4 51 f4 56 97 75 10*0 4 51 4 52 24 56 97 75
  //   8*0 4 51 4 52 f6 28 74 56 97 75 6*0 4 51 f6 97 7f 11*0 4 51 14*0 4 51 14*0 4 51 14*0 4 51 14*0 4 51
  //   14*0 4 51 14*0 4 51 14*0 4 51 14*0 4 51 14*0 4 51 14*0 4 51 14*0 4 51 14*0 4 51 14*0 4 51 14*0 4 51
  //   14*0 4 51 14*0 4 51 1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
endmodule

module constants (
  input  intinstout,
  input  intaddrout,
  input  zeroout,
  output [15:0] data
);

  assign data = zeroout ? {16{1'b0}} : 16'bz;  // Controlled_Buffer controlled_buffer_1
  assign data = intaddrout ? 16'hd720 : 16'bz;  // Controlled_Buffer controlled_buffer_2
  // Probe on data
  assign data = intinstout ? ~16'h3f00 : 16'bz;  // Controlled_Inverter controlled_inverter_1
endmodule

module alu (
  input  zinadd,
  input  [3:0] ir,
  input  yin,
  input  clock,
  input  aclr,
  input  zin,
  input  zout,
  input  [15:0] data,
  output cout,
  output overflow,
  output parity,
  output zero,
  output sign,
  output [15:0] qbus
);

  wire decoder_1_out0, decoder_1_out1, decoder_1_out4, decoder_1_out5, decoder_1_out6, decoder_1_out7,
       decoder_1_out8, decoder_1_out9, decoder_1_out10, decoder_1_out11, not_1_out, or_1_out, or_2_out,
       or_3_out, or_4_out;
  wire [14:0] add_sub_1_result;
  wire [15:0] register_1_q, register_2_q;

  Register #(.width(16)) register_1 (.D(data), .en(yin), .clk(clock), .Q(register_1_q), .clr(aclr));
  not not_1 (not_1_out, zinadd);
  Decoder #(.select(4)) decoder_1 (
    .out0(decoder_1_out0), .out1(decoder_1_out1), .out4(decoder_1_out4), .out5(decoder_1_out5),
    .out6(decoder_1_out6), .out7(decoder_1_out7), .out8(decoder_1_out8), .out9(decoder_1_out9),
    .out10(decoder_1_out10), .out11(decoder_1_out11), .sel(ir), .en(not_1_out));  // open: out2, out3, out12, out13, out14, out15
  or or_1 (or_1_out, decoder_1_out0, decoder_1_out8, decoder_1_out11, zinadd);
  or or_2 (or_2_out, decoder_1_out0, decoder_1_out5, decoder_1_out7, decoder_1_out8, decoder_1_out9, decoder_1_out10, decoder_1_out11, zinadd);
  or or_3 (or_3_out, decoder_1_out5, decoder_1_out7, decoder_1_out8, decoder_1_out11);
  or or_4 (or_4_out, zin, zinadd);
  add_sub add_sub_1 (
    .dataa(register_1_q), .cin(or_3_out), .enable(or_2_out), .dir(or_1_out), .datab(data),
    .result({sign, add_sub_1_result}), .cout(cout), .overflow(overflow));
  orgate orgate_1 (.dataa(register_1_q), .datab(data), .enable(decoder_1_out1), .result({sign, add_sub_1_result}));
  andgate andgate_1 (.dataa(register_1_q), .datab(data), .enable(decoder_1_out4), .result({sign, add_sub_1_result}));
  xorgate xorgate_1 (.dataa(register_1_q), .datab(data), .enable(decoder_1_out6), .result({sign, add_sub_1_result}));
  Register #(.width(16)) register_2 (
    .D({sign, add_sub_1_result}), .en(or_4_out), .clk(clock), .Q(register_2_q), .clr(aclr));
  assign qbus = zout ? register_2_q : 16'bz;  // Controlled_Buffer controlled_buffer_1
  xnor xnor_1 (parity, add_sub_1_result[0], add_sub_1_result[1], add_sub_1_result[2], add_sub_1_result[3], add_sub_1_result[4], add_sub_1_result[5], add_sub_1_result[6], add_sub_1_result[7], add_sub_1_result[8], add_sub_1_result[9], add_sub_1_result[10], add_sub_1_result[11], add_sub_1_result[12], add_sub_1_result[13], add_sub_1_result[14], sign);
  nor nor_1 (zero, add_sub_1_result[0], add_sub_1_result[1], add_sub_1_result[2], add_sub_1_result[3], add_sub_1_result[4], add_sub_1_result[5], add_sub_1_result[6], add_sub_1_result[7], add_sub_1_result[8], add_sub_1_result[9], add_sub_1_result[10], add_sub_1_result[11], add_sub_1_result[12], add_sub_1_result[13], add_sub_1_result[14], sign);

  // Notes on the sheet:
  //   parity: pull=down
  //   zero: pull=down
  //   sign: pull=down
endmodule

module add_sub (
  input  [15:0] dataa,
  input  cin,
  input  enable,
  input  dir,
  input  [15:0] datab,
  output [15:0] result,
  output cout,
  output overflow
);

  wire xor_2_out, xor_3_out, xor_4_out;
  wire [14:0] adder_1_out_2;
  wire [15:0] xor_1_out;
  wire [16:0] adder_1_out;

  assign xor_1_out = ~{16{dir}} ^ datab;  // XOR_Gate xor_1, 16 bits wide
  xor xor_2 (xor_2_out, dataa[15], datab[15]);
  Adder #(.width(18)) adder_1 (
    .a({1'b0, dataa, cin}), .b({1'b0, xor_1_out, cin}),
    .out({cout, adder_1_out[16], adder_1_out_2, adder_1_out[0]}), .cin(1'b0));  // open: cout
  xor xor_3 (xor_3_out, dataa[15], adder_1_out[16]);
  xor xor_4 (xor_4_out, ~xor_2_out, ~dir);  // XOR_Gate
  assign result = enable ? {adder_1_out[16], adder_1_out_2} : 16'bz;  // Controlled_Buffer controlled_buffer_1
  and and_1 (overflow, xor_3_out, xor_4_out);
endmodule

module orgate (
  input  [15:0] dataa,
  input  [15:0] datab,
  input  enable,
  output [15:0] result
);

  wire [15:0] or_1_out;

  assign or_1_out = dataa | datab;  // OR_Gate or_1, 16 bits wide
  assign result = enable ? or_1_out : 16'bz;  // Controlled_Buffer controlled_buffer_1
endmodule

module andgate (
  input  [15:0] dataa,
  input  [15:0] datab,
  input  enable,
  output [15:0] result
);

  wire [15:0] and_1_out;

  assign and_1_out = dataa & datab;  // AND_Gate and_1, 16 bits wide
  assign result = enable ? and_1_out : 16'bz;  // Controlled_Buffer controlled_buffer_1
endmodule

module xorgate (
  input  [15:0] dataa,
  input  [15:0] datab,
  input  enable,
  output [15:0] result
);

  wire [15:0] xor_1_out;

  assign xor_1_out = dataa ^ datab;  // XOR_Gate xor_1, 16 bits wide
  assign result = enable ? xor_1_out : 16'bz;  // Controlled_Buffer controlled_buffer_1
endmodule

module cpu (
  input  clock,
  input  aclr,
  input  busy,
  input  intr,
  output marin,
  output ramin,
  output ramout
);

  wire and_1_out, and_2_out, control_unit_1_ucounterrst, jump_controller_1_jump_enable, or_1_out, or_2_out;
  wire [3:0] ir1_q_2;
  wire [10:0] bit_extender_1_out;
  wire [11:0] alu_1_cout;
  wire [15:0] alu_1_qbus, ax_q, flags_register_1_q, ir1_q;
  wire [47:0] control_unit_1_control;

  control_unit control_unit_1 (
    .ir({ir1_q[15:12], ir1_q_2, ir1_q[7:0]}), .clock(clock), .aclr(aclr), .busy(busy),
    .control({control_unit_1_control[47:22], ramout, control_unit_1_control[20:6], ramin, marin, control_unit_1_control[3:0]}),
    .ucounterrst(control_unit_1_ucounterrst));
  and and_1 (and_1_out, control_unit_1_ucounterrst, intr);
  or or_1 (or_1_out, control_unit_1_control[1], and_1_out);
  jump_controller jump_controller_1 (
    .flags(flags_register_1_q), .pcinun(control_unit_1_control[11]), .pcin(control_unit_1_control[0]),
    .ir(ir1_q_2), .jump_enable(jump_controller_1_jump_enable));
  alu alu_1 (
    .zinadd(control_unit_1_control[8]), .ir({ir1_q[14:12], ir1_q_2[3]}), .yin(control_unit_1_control[6]),
    .clock(clock), .aclr(aclr), .zin(control_unit_1_control[7]), .zout(control_unit_1_control[23]),
    .data(alu_1_qbus), .cout(alu_1_cout[0]), .overflow(alu_1_cout[11]), .parity(alu_1_cout[2]),
    .zero(alu_1_cout[6]), .sign(alu_1_cout[7]), .qbus(alu_1_qbus));
  assign bit_extender_1_out = {{10{1'b0}}, 1'b0};  // Bit_Extender bit_extender_1
  or or_2 (or_2_out, or_1_out, control_unit_1_control[2], control_unit_1_control[3]);
  and and_2 (and_2_out, or_2_out, ramout);
  reg16 ir1 (
    .regout(control_unit_1_control[17]), .data(alu_1_qbus), .regin(or_1_out), .clock(clock), .aclr(aclr),
    .q({ir1_q[15:12], ir1_q_2, ir1_q[7:0]}), .qbus(alu_1_qbus));
  flags_register flags_register_1 (
    .flagsout(control_unit_1_control[28]),
    .flags({bit_extender_1_out[10:7], alu_1_cout[11], bit_extender_1_out[6:4], alu_1_cout[7:6], bit_extender_1_out[3:1], alu_1_cout[2], bit_extender_1_out[0], alu_1_cout[0]}),
    .data(alu_1_qbus), .flagsin(control_unit_1_control[12]), .zin(control_unit_1_control[7]), .clock(clock),
    .aclr(aclr), .q(flags_register_1_q), .qbus(alu_1_qbus));
  program_counter program_counter_1 (
    .aclr(aclr), .pcin(jump_controller_1_jump_enable), .cnt_en(and_2_out), .clock(clock),
    .pcout(control_unit_1_control[16]), .data(alu_1_qbus), .q(alu_1_qbus));
  reg16 ir2 (
    .regout(control_unit_1_control[18]), .data(alu_1_qbus), .regin(control_unit_1_control[2]), .clock(clock),
    .aclr(aclr), .qbus(alu_1_qbus));  // open: q
  reg16 ir3 (
    .regout(control_unit_1_control[19]), .data(alu_1_qbus), .regin(control_unit_1_control[3]), .clock(clock),
    .aclr(aclr), .qbus(alu_1_qbus));  // open: q
  reg16 ax (
    .regout(control_unit_1_control[40]), .data(alu_1_qbus), .regin(control_unit_1_control[32]),
    .clock(clock), .aclr(aclr), .q(ax_q), .qbus(alu_1_qbus));
  reg16 cx (
    .regout(control_unit_1_control[41]), .data(alu_1_qbus), .regin(control_unit_1_control[33]),
    .clock(clock), .aclr(aclr), .qbus(alu_1_qbus));  // open: q
  reg16 dx (
    .regout(control_unit_1_control[42]), .data(alu_1_qbus), .regin(control_unit_1_control[34]),
    .clock(clock), .aclr(aclr), .qbus(alu_1_qbus));  // open: q
  reg16 bx (
    .regout(control_unit_1_control[43]), .data(alu_1_qbus), .regin(control_unit_1_control[35]),
    .clock(clock), .aclr(aclr), .qbus(alu_1_qbus));  // open: q
  reg16 sp (
    .regout(control_unit_1_control[44]), .data(alu_1_qbus), .regin(control_unit_1_control[36]),
    .clock(clock), .aclr(aclr), .qbus(alu_1_qbus));  // open: q
  reg16 bp (
    .regout(control_unit_1_control[45]), .data(alu_1_qbus), .regin(control_unit_1_control[37]),
    .clock(clock), .aclr(aclr), .qbus(alu_1_qbus));  // open: q
  reg16 si (
    .regout(control_unit_1_control[46]), .data(alu_1_qbus), .regin(control_unit_1_control[38]),
    .clock(clock), .aclr(aclr), .qbus(alu_1_qbus));  // open: q
  reg16 di (
    .regout(control_unit_1_control[47]), .data(alu_1_qbus), .regin(control_unit_1_control[39]),
    .clock(clock), .aclr(aclr), .qbus(alu_1_qbus));  // open: q
  reg16 temp (
    .regout(control_unit_1_control[26]), .data(alu_1_qbus), .regin(control_unit_1_control[10]),
    .clock(clock), .aclr(aclr), .qbus(alu_1_qbus));  // open: q
  constants constants_1 (
    .intinstout(and_1_out), .intaddrout(control_unit_1_control[20]), .zeroout(control_unit_1_control[25]),
    .data(alu_1_qbus));
  // Probe on alu_1_qbus
  Hex_Digit_Display hex_digit_display_1 (.value(ax_q[15:12]));  // open: dp
  Hex_Digit_Display hex_digit_display_2 (.value(ax_q[11:8]));  // open: dp
  memory memory_1 (
    .data(alu_1_qbus), .ramin(ramin), .marin(marin), .clock(clock), .aclr(aclr), .ramout(ramout),
    .q(alu_1_qbus));
  Hex_Digit_Display hex_digit_display_3 (.value(ax_q[7:4]));  // open: dp
  Hex_Digit_Display hex_digit_display_4 (.value(ax_q[3:0]));  // open: dp
endmodule

module memory (
  input  [15:0] data,
  input  ramin,
  input  marin,
  input  clock,
  input  aclr,
  input  ramout,
  output [15:0] q
);

  wire and_1_out, nor_1_out;
  wire [15:0] controlled_buffer_1_out, ram_1_dout, register_1_q, rom_1_data;

  Register #(.width(16)) register_1 (.D(data), .en(marin), .clk(clock), .Q(register_1_q), .clr(aclr));
  nor nor_1 (nor_1_out, register_1_q[15], register_1_q[14]);
  ROM #(.addrWidth(14), .dataWidth(16)) rom_1 (.addr(register_1_q[13:0]), .data(rom_1_data));
  assign controlled_buffer_1_out = nor_1_out ? rom_1_data : 16'bz;  // Controlled_Buffer controlled_buffer_1
  RAM #(.addrWidth(14), .asyncread("true"), .dataWidth(16)) ram_1 (
    .addr(register_1_q[13:0]), .we(ramin), .oe(1'b1), .clk(clock), .din(data), .dout(ram_1_dout));
  and and_1 (and_1_out, ~register_1_q[15], register_1_q[14]);  // AND_Gate
  assign controlled_buffer_1_out = and_1_out ? ram_1_dout : 16'bz;  // Controlled_Buffer controlled_buffer_2
  assign q = ramout ? controlled_buffer_1_out : 16'bz;  // Controlled_Buffer controlled_buffer_3

  // Notes on the sheet:
  //   contents of rom_1 (hex, n*v repeats v):
  //   8dc4 7ffe 8dc1 7ad0 8dc2 100 8911 8dc0 1111 d021 8dc0 7777 2dc1 77d0 d0e1 8dc0 bbbb 239*0 8dc0 2222
  //   d060 300 8dc0 4444 d060 200 8dc0 6666 d820 245*0 8dc0 5555 d820 253*0 8dc0 3333 d820 253*0 8dc0 8888
  //   d060 500 8dc0 aaaa d820 249*0 8dc0 9999 d820
endmodule
