// Logisim project program_counter.circ as structural Verilog
module main (
  input  aclr,
  input  pcin,
  input  cnt_en,
  input  clock,
  input  pcout,
  input  [15:0] data,
  output [15:0] q
);

  // Probe on data
  assign data = pcout ? q : 16'bz;  // Controlled_Buffer controlled_buffer_1
  Counter #(.max('hffff), .width(16)) counter_1 (
    .clr(aclr), .load(pcin), .up(1'b1), .count(cnt_en), .clk(clock), .D(data), .Q(q));  // open: carry
  Hex_Digit_Display hex_digit_display_1 (.value(q[11:8]));  // open: dp
  Hex_Digit_Display hex_digit_display_2 (.value(q[15:12]));  // open: dp
  Hex_Digit_Display hex_digit_display_3 (.value(q[7:4]));  // open: dp
  Hex_Digit_Display hex_digit_display_4 (.value(q[3:0]));  // open: dp
endmodule
