// Logisim project reg.circ as structural Verilog: 1 circuit, main circuit main
module main (
  input  regout,
  input  [15:0] data,
  input  regin,
  input  clock,
  input  aclr,
  output [15:0] q
);

  assign data = regout ? q : 16'bz;  // Controlled_Buffer controlled_buffer_1
  Register #(.width(16)) register_1 (.D(data), .en(regin), .clk(clock), .Q(q), .clr(aclr));
  Hex_Digit_Display hex_digit_display_1 (.value(q[15:12]));  // open: dp
  Hex_Digit_Display hex_digit_display_2 (.value(q[11:8]));  // open: dp
  Hex_Digit_Display hex_digit_display_3 (.value(q[7:4]));  // open: dp
  Hex_Digit_Display hex_digit_display_4 (.value(q[3:0]));  // open: dp
endmodule
